# Fritzing sketch Sistem monitoring tegangan PLTA (saved by Fritzing 0.8.7b)

parts:
  U1 = ESP8266 ESP-01 Upgraded WiFi Module [part_number=ESP8266]
  Part1 = Arduino Uno (Rev3)
  Driver1 = 28BYJ-48 Driver Module [part_number=ULN2003 package=THT]
  SM1 = 28BYJ-48 Stepper Motor [part_number=28BYJ-48]
  Part2 = SRF05 Ultrasonic Rangefinder
  M1 = DC Motor
  S1 = Pushbutton [package="[THT]"]
  S2 = Pushbutton [package="[THT]"]

nets:
  N1: U1.RXD, Part1.D1/TX
  VCC: U1.VCC, Part1.3V3
  GND: U1.RST/GPIO_16, U1.CH_PD, U1.GND, Part1.GND, M1.pin_2, S1.Pin_1, S1.Pin_2
  N2: U1.TXD, Part1.D0/RX
  N3: Part1.A0, M1.pin_1
  N4: Part1.D8, Driver1.IN4
  N5: Part1.D9_PWM, Driver1.IN3
  N6: Part1.D10_PWM/SS, Driver1.IN2
  N7: Part1.D11_PWM/MOSI, Driver1.IN1
  N8: Part1.D2, Part1.D3_PWM, S2.Pin_3, S2.Pin_4
  N9: Part1.D4, Part2.GND
  N10: Part1.D5_PWM, Part2.Echo
  N11: Part1.D6_PWM, Part2.Trig
  N12: Part1.D7, Part2.VCC
  N13: Driver1.blue-pin, SM1.blue-pin
  N14: Driver1.pink-pin, SM1.pink-pin
  N15: Driver1.yellow-pin, SM1.yellow-pin
  N16: Driver1.orange-pin, SM1.orange-pin
  N17: Driver1.red-pin, SM1.red-pin

custom parts:
  ESP8266 ESP-01 Upgraded WiFi Module: Upgraded Version ESP-01,all Flash are upgraded to 1M byte.Also support Cloud service remote transmission.
  28BYJ-48 Driver Module: ULN2003 Driver Module for the 28BYJ-48 Unipolar Stepper Motor LED A - Blue wire - Bottom coil left LED B - Pink wire - Top coil left LED C - Yellow wire - Bottom coil right LED D - Orange wire - Top coil right Common rail - red Connector pins: blue - pink - yellow - orange - red Control pins - IN1 to IN4 Power pins - GND & Vmotor (5-12V) On/Off jumper (if removed, power to motor is cut).
  28BYJ-48 Stepper Motor: Unipolar Stepper Motor 28BYJ-48 Top coil - pink & orange Bottom coil - blue & yellow Common rail - red Connector pins: blue - pink - yellow - orange - red
