# Fritzing sketch Skema rangkaian (saved by Fritzing 0.8.7b)

parts:
  Part2 = RFID-RC522-v2
  J1 = Piezo Speaker
  LED1 = LED - 5mm [color="Red (633nm)" package="5 mm [THT]"]
  LED2 = LED - 5mm [color="Red (633nm)" package="5 mm [THT]"]
  LED3 = LED - 5mm [color="Red (633nm)" package="5 mm [THT]"]
  LED4 = LED - 5mm [color="Red (633nm)" package="5 mm [THT]"]
  LED5 = LED - 5mm [color="Red (633nm)" package="5 mm [THT]"]
  LED6 = LED - 5mm [color="Red (633nm)" package="5 mm [THT]"]
  U1 = LCD-16X2 [package=lcd-16x2]
  LCM1602_IIC1 = LCM1602 IIC [part_number="LCM1602 IIC" chip_label="LCM1602 IIC" package="DIP (Dual Inline) [THT]"]
  J2 = Basic Servo
  Keyes1 = Keyes IR Infrared Sensor Switch Module  # not connected
  R2 = Resistor [tolerance=±5% resistance=220 package=THT]
  R3 = Resistor [tolerance=±5% resistance=220 package=THT]
  R4 = Resistor [tolerance=±5% resistance=220 package=THT]
  R5 = Resistor [tolerance=±5% resistance=220 package=THT]
  R6 = Resistor [tolerance=±5% resistance=220 package=THT]
  R7 = Resistor [tolerance=±5% resistance=220 package=THT]
  Part3 = SRF05 Ultrasonic Rangefinder
  Part4 = Arduino Mega ADK (Rev3)
  Keyes2 = Keyes IR Infrared Sensor Switch Module  # not connected
  Keyes3 = Keyes IR Infrared Sensor Switch Module  # not connected
  Keyes4 = Keyes IR Infrared Sensor Switch Module  # not connected
  Keyes5 = Keyes IR Infrared Sensor Switch Module  # not connected
  Keyes6 = Keyes IR Infrared Sensor Switch Module  # not connected

nets:
  N1: Part2.SDA, Part4.D53/SS
  N2: Part2.SCK, Part4.D52/SCK
  N3: Part2.MOSI, Part4.D51/MOSI
  N4: Part2.MISO, Part4.D50/MISO
  GND: Part2.GND, J1.pin2, LED1.cathode, LED2.cathode, LED3.cathode, LED4.cathode, LED5.cathode, LED6.cathode, LCM1602_IIC1.GND, J2.gnd, Part3.GND, Part4.GND
  N5: Part2.RST, Part4.D5_PWM
  3.3V: Part2.3.3V, Part4.3V3
  N6: J1.pin1, Part4.AREF
  VSS: U1.VSS, LCM1602_IIC1.VSS
  VDD: U1.VDD, LCM1602_IIC1.VDD
  N7: U1.VO, LCM1602_IIC1.V0
  N8: U1.RS, LCM1602_IIC1.RS
  N9: U1.R_W, LCM1602_IIC1.RW
  N10: U1.E, LCM1602_IIC1.E
  N11: U1.DB0, LCM1602_IIC1.D0
  N12: U1.DB1, LCM1602_IIC1.D1
  N13: U1.DB2, LCM1602_IIC1.D2
  N14: U1.DB3, LCM1602_IIC1.D3
  N15: U1.DB4, LCM1602_IIC1.D4
  N16: U1.DB5, LCM1602_IIC1.D5
  N17: U1.DB6, LCM1602_IIC1.D6
  N18: U1.DB7, LCM1602_IIC1.D7
  N19: U1.A, LCM1602_IIC1.A
  N20: U1.K, LCM1602_IIC1.K
  VCC: LCM1602_IIC1.VCC, Part3.VCC, Part4.5V
  N21: LCM1602_IIC1.LED_A, LCM1602_IIC1.LED_B
  N22: J2.pulse, Part4.D7_PWM
  N23: R2.Pin_0, Part4.D8_PWM
  N24: R3.Pin_0, Part4.D9_PWM
  N25: R4.Pin_0, Part4.D10_PWM
  N26: R5.Pin_0, Part4.D11_PWM
  N27: R6.Pin_0, Part4.D12_PWM
  N28: R7.Pin_0, Part4.D13_PWM
  N29: Part3.Trig, Part4.D4_PWM
  N30: Part3.Echo, Part4.D3_PWM

custom parts:
  RFID-RC522-v2: A simple China made RFID-RC522 Reader; do check the pin labels, as this is a MFRC522 based clone.
  LCM1602 IIC: I2C-Module to use a 1602 or 2004 LCD on with the wire.h libory Serial LCD Modul
  Keyes IR Infrared Sensor Switch Module: An infrared obstacle detector
