# Fritzing sketch Untitled Sketch (saved by Fritzing 0.9.3b)

parts:
  U1 = 2-Channel 5v Relay Shield [package=relay-2ch5v10a]
  L1 = Solenoid
  L2 = Solenoid
  VCC1 = Battery
  U2 = LM2596 step down module
  U3 = ESP 32 DEVKIT DOIT
  JL012-13-5_1 = JL012-13-5.2 Lever (Limit) Switch SPDT + NO + NC [part_number=JL012-13-5.2]
  R1 = Resistor [tolerance=±5% resistance=220 package=THT]
  R2 = Resistor [tolerance=±5% resistance=220 package=THT]
  JL012-13-5_2 = JL012-13-5.2 Lever (Limit) Switch SPDT + NO + NC [part_number=JL012-13-5.2]
  KEYPAD1 = Membrane Matrix Keypad
  Part1 = HC-SR04
  LED2 = LED - 5mm [color="Red (633nm)" package="5 mm [THT]"]
  R3 = Resistor [tolerance=±5% resistance=220 package=THT]
  U4 = LCD-16X2 [package=lcd-16x2]
  LCM1602_IIC1 = LCM1602 IIC [part_number="LCM1602 IIC" chip_label="LCM1602 IIC" package="DIP (Dual Inline) [THT]"]

nets:
  N1: U1.IN1, U1.IN2, U3.D22, U3.D18, U3.D5, U3.RX2, U3.D4, U3.D2, U3.SD1, Part1.Trig, R3.Pin_1, LCM1602_IIC1.SCL
  N2: U1.K1-In, L2.pin2
  N3: U1.K1-On, U1.K2-On
  N4: U1.K2-In, L1.pin2
  N5: VCC1.+, U2.IN+
  N6: U2.OUT+, U3.VIN
  N7: U3.D21, LCM1602_IIC1.SDA
  N8: U3.D19, Part1.Echo
  N9: U3.GND, JL012-13-5_1.NO, LED2.cathode
  N10: U3.D13, KEYPAD1.1
  N11: U3.D12, KEYPAD1.2
  N12: U3.D14, KEYPAD1.3
  N13: U3.D27, KEYPAD1.4
  N14: U3.D26, KEYPAD1.5
  N15: U3.D25, KEYPAD1.6
  N16: U3.D33, KEYPAD1.7
  N17: U3.VN, R2.Pin_1, JL012-13-5_2.C
  N18: U3.VP, JL012-13-5_1.C, R1.Pin_1
  N19: R1.Pin_0, R2.Pin_0
  VSS: U4.VSS, LCM1602_IIC1.VSS
  VDD: U4.VDD, LCM1602_IIC1.VDD
  N20: U4.VO, LCM1602_IIC1.V0
  N21: U4.RS, LCM1602_IIC1.RS
  N22: U4.R_W, LCM1602_IIC1.RW
  N23: U4.E, LCM1602_IIC1.E
  N24: U4.DB0, LCM1602_IIC1.D0
  N25: U4.DB1, LCM1602_IIC1.D1
  N26: U4.DB2, LCM1602_IIC1.D2
  N27: U4.DB3, LCM1602_IIC1.D3
  N28: U4.DB4, LCM1602_IIC1.D4
  N29: U4.DB5, LCM1602_IIC1.D5
  N30: U4.DB6, LCM1602_IIC1.D6
  N31: U4.DB7, LCM1602_IIC1.D7
  N32: U4.A, LCM1602_IIC1.A
  N33: U4.K, LCM1602_IIC1.K
  N34: LCM1602_IIC1.LED_A, LCM1602_IIC1.LED_B

custom parts:
  2-Channel 5v Relay Shield: 2 Channel 5v Relay Shield w. 2x SPD-06VDC-SD-C
  Battery: Your standard 2x 18650 battery pack (7,4 Volts)
  LM2596 step down module: LM2596 DC-DC step down power supply module 3 A.
  JL012-13-5.2 Lever (Limit) Switch SPDT + NO + NC: Micro Switch; Model No.: JL012-13.5-2; Actuator Action: Momentary; Actuator Type: Hinge Lever; Contact Configuration: 1NO, 1NC (SPDT) Temperature -25~65℃；Relative humidity: below 85%; Rate Voltage: 125V AC; Rated Current: 1A.
  Membrane Matrix Keypad: Membrane Matrix 3x4 Keypad
  HC-SR04: HC-SR04 ultrasonic distance sensor
  LCM1602 IIC: I2C-Module to use a 1602 or 2004 LCD on with the wire.h libory Serial LCD Modul
