# Fritzing sketch Untitled Sketch (saved by Fritzing 0.9.3b)

parts:
  J1 = Basic Force Sensing Resistor (FSR) [package=THT]
  J2 = Basic Force Sensing Resistor (FSR) [package=THT]
  J3 = Basic Force Sensing Resistor (FSR) [package=THT]
  J4 = Basic Force Sensing Resistor (FSR) [package=THT]
  J5 = Basic Force Sensing Resistor (FSR) [package=THT]
  R1 = Resistor [tolerance=±5% resistance=220 package=THT]
  Part1 = Arduino Nano (Rev3.0)
  R2 = Resistor [tolerance=±5% resistance=220 package=THT]
  R3 = Resistor [tolerance=±5% resistance=220 package=THT]
  R4 = Resistor [tolerance=±5% resistance=220 package=THT]
  R5 = Resistor [tolerance=±5% resistance=220 package=THT]
  U1 = LCD-16X2 [package=lcd-16x2]
  LCM1602_IIC2 = LCM1602 IIC [part_number="LCM1602 IIC" chip_label="LCM1602 IIC" package="DIP (Dual Inline) [THT]"]
  HC-SR04_Sensor_1 = HC-SR04 Ultrasonic Distance Sensor
  HC-SR04_Sensor_2 = HC-SR04 Ultrasonic Distance Sensor
  HC-SR04_Sensor_3 = HC-SR04 Ultrasonic Distance Sensor
  HC-SR04_Sensor_4 = HC-SR04 Ultrasonic Distance Sensor
  S1 = Square Pushbutton
  S2 = Square Pushbutton
  S3 = Square Pushbutton

nets:
  N1: J1.pin_1, Part1.A3, R2.Pin_1
  N2: J2.pin_1, R3.Pin_1
  N3: J3.pin_1, Part1.A1, R4.Pin_1
  N4: J4.pin_1, Part1.A0, R5.Pin_1
  N5: J5.pin_1, R1.Pin_1
  GND: R1.Pin_0, R5.Pin_0, HC-SR04_Sensor_1.GND, HC-SR04_Sensor_3.GND
  N6: Part1.D2, HC-SR04_Sensor_1.TRIG
  N7: Part1.D3, HC-SR04_Sensor_1.ECHO
  N8: Part1.D4, HC-SR04_Sensor_2.TRIG
  N9: Part1.D5, HC-SR04_Sensor_2.ECHO
  N10: Part1.D6, HC-SR04_Sensor_3.TRIG
  N11: Part1.D7, HC-SR04_Sensor_3.ECHO
  N12: Part1.D8, HC-SR04_Sensor_4.TRIG
  N13: Part1.D9, HC-SR04_Sensor_4.ECHO
  N14: Part1.D10, S2.leg1
  N15: Part1.D11/MOSI, S1.leg1
  N16: Part1.D12/MISO, S3.leg1
  GND_2: Part1.GND, LCM1602_IIC2.GND
  5V: Part1.5V, LCM1602_IIC2.VCC
  N17: Part1.A5, LCM1602_IIC2.SCL
  N18: Part1.A4, LCM1602_IIC2.SDA
  VSS: U1.VSS, LCM1602_IIC2.VSS
  VDD: U1.VDD, LCM1602_IIC2.VDD
  N19: U1.VO, LCM1602_IIC2.V0
  N20: U1.RS, LCM1602_IIC2.RS
  N21: U1.R_W, LCM1602_IIC2.RW
  N22: U1.E, LCM1602_IIC2.E
  N23: U1.DB0, LCM1602_IIC2.D0
  N24: U1.DB1, LCM1602_IIC2.D1
  N25: U1.DB2, LCM1602_IIC2.D2
  N26: U1.DB3, LCM1602_IIC2.D3
  N27: U1.DB4, LCM1602_IIC2.D4
  N28: U1.DB5, LCM1602_IIC2.D5
  N29: U1.DB6, LCM1602_IIC2.D6
  N30: U1.DB7, LCM1602_IIC2.D7
  N31: U1.A, LCM1602_IIC2.A
  N32: U1.K, LCM1602_IIC2.K
  N33: LCM1602_IIC2.LED_A, LCM1602_IIC2.LED_B
  VCC: HC-SR04_Sensor_1.VCC, HC-SR04_Sensor_3.VCC
  N34: S2.leg0, S3.leg0

custom parts:
  LCM1602 IIC: I2C-Module to use a 1602 or 2004 LCD on with the wire.h libory Serial LCD Modul
