# Fritzing sketch Untitled Sketch (saved by Fritzing 0.9.3b)

parts:
  Jetson_Nano3 = Jetson Nano
  KY-1 = Keyes Relay [package=THT]
  M2 = DC Motor
  Part1 = Adafruit BMP280 [part_number="Adafruit #2651"]
  VCC1 = 4 x AAA Battery Mount

nets:
  N1: Jetson_Nano3.GPIO11, KY-1.signal
  N2: Jetson_Nano3.GPIO19, Part1.GND
  N3: Jetson_Nano3.GPIO26, Part1.VCC
  N4: Jetson_Nano3.GPIO20, Part1.SDI/SDA
  N5: Jetson_Nano3.GPIO16, Part1.SCK/SCL
  N6: KY-1.C, M2.pin_1
  N7: KY-1.NO, VCC1.+
  N8: M2.pin_2, VCC1.-

custom parts:
  Keyes Relay: The Keyes 5V relay module is suitable for SCM development, home appliance control. It uses a 5V~12V TIL control signal which can control DC / AC signal.
  Adafruit BMP280: Bosch has stepped up their game with their new BMP280 sensor, an environmental sensor with temperature, barometric pressure that is the next generation upgrade to the BMP085/BMP180/BMP183. This sensor is great for all sorts of weather sensing and can even be used in both I2C and SPI! This precision sensor from Bosch is the best low-cost, precision sensing solution for measuring barometric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
